// Logisim project processor made from 74 series.circ as structural Verilog
// 195
module _74ls195 (
  input  Clock,
  input  clear,
  input  [3:0] Parallel_In,
  input  J,
  input  Parallel_Load,
  output nQ3,
  output [3:0] Parallel_Out
);

  wire and_1_out, and_2_out, and_3_out, and_4_out, and_5_out, and_6_out, and_7_out, and_8_out, and_9_out,
       nor_1_out, nor_2_out, nor_3_out, nor_4_out, not_1_out, not_2_out, not_3_out, not_4_out, not_5_out,
       not_6_out, not_7_out, s_r_ff_1_qn;

  not not_1 (not_1_out, Parallel_Load);
  not not_2 (not_2_out, not_1_out);
  and and_1 (and_1_out, s_r_ff_1_qn, J, not_2_out);
  and and_2 (and_2_out, not_2_out, J, Parallel_Out[0]);
  and and_3 (and_3_out, not_1_out, Parallel_In[0]);
  not not_3 (not_3_out, nor_1_out);
  nor nor_1 (nor_1_out, and_1_out, and_2_out, and_3_out);
  and and_4 (and_4_out, Parallel_Out[0], not_2_out);
  nor nor_2 (nor_2_out, and_4_out, and_5_out);
  S_R_Flip_Flop s_r_ff_1 (
    .S(not_3_out), .clk(Clock), .R(nor_1_out), .Q(Parallel_Out[0]), .Qn(s_r_ff_1_qn), .reset(not_7_out));  // open: preset, en
  and and_5 (and_5_out, not_1_out, Parallel_In[1]);
  S_R_Flip_Flop s_r_ff_2 (
    .S(not_4_out), .clk(Clock), .R(nor_2_out), .Q(Parallel_Out[1]), .reset(not_7_out));  // open: Qn, preset, en
  not not_4 (not_4_out, nor_2_out);
  and and_6 (and_6_out, Parallel_Out[1], not_2_out);
  and and_7 (and_7_out, not_1_out, Parallel_In[2]);
  nor nor_3 (nor_3_out, and_6_out, and_7_out);
  not not_5 (not_5_out, nor_3_out);
  S_R_Flip_Flop s_r_ff_3 (
    .S(not_5_out), .clk(Clock), .R(nor_3_out), .Q(Parallel_Out[2]), .reset(not_7_out));  // open: Qn, preset, en
  and and_8 (and_8_out, Parallel_Out[2], not_2_out);
  and and_9 (and_9_out, not_1_out, Parallel_In[3]);
  nor nor_4 (nor_4_out, and_8_out, and_9_out);
  not not_6 (not_6_out, nor_4_out);
  S_R_Flip_Flop s_r_ff_4 (
    .S(not_6_out), .clk(Clock), .R(nor_4_out), .Q(Parallel_Out[3]), .Qn(nQ3), .reset(not_7_out));  // open: preset, en
  not not_7 (not_7_out, clear);
endmodule

module procesor_idea_1 (
  input  in_1,
  input  in_2,
  input  [7:0] in_3,
  output [3:0] out_4,
  output [3:0] out_5,
  output [3:0] out_6,
  output [7:0] out_7
);

  wire and_1_out, clock_1_out, counter_1_carry, decoder_1_out0, decoder_1_out1, decoder_1_out2,
       decoder_1_out3, n74ls195_1_nq3, n74ls195_3_nq3, nand_1_out, not_1_out, not_2_out, not_3_out;
  wire [3:0] counter_2_q, counter_2_q_2;
  wire [7:0] counter_1_q;

  not not_1 (not_1_out, n74ls195_3_nq3);
  Counter counter_1 (
    .load(decoder_1_out0), .D(out_7), .count(not_3_out), .Q(counter_1_q), .carry(counter_1_carry),
    .clk(clock_1_out), .clr(in_2));
  Counter counter_2 (
    .load(decoder_1_out1), .D(counter_1_q), .count(not_3_out), .Q({counter_2_q_2, counter_2_q}),
    .clk(counter_1_carry), .clr(in_2));  // open: carry
  _74ls195 u_74ls195_1 (
    .Clock(and_1_out), .clear(in_2), .Parallel_In(counter_2_q_2), .J(not_1_out),
    .Parallel_Load(decoder_1_out2), .Parallel_Out(out_4), .nQ3(n74ls195_1_nq3));
  not not_2 (not_2_out, n74ls195_1_nq3);
  _74ls195 u_74ls195_2 (
    .Clock(and_1_out), .clear(in_2), .Parallel_In(counter_2_q), .J(not_2_out),
    .Parallel_Load(decoder_1_out2), .Parallel_Out(out_5));  // open: nQ3
  // _74ls189 74ls189_1: pin names not known; wires that end beside it: out_5, 1'b0, out_7[3:0]
  _74ls195 u_74ls195_3 (
    .Clock(and_1_out), .clear(in_2), .Parallel_In(out_7[3:0]), .Parallel_Load(decoder_1_out3),
    .Parallel_Out(out_7[7:4]), .nQ3(n74ls195_3_nq3));  // open: J
  ROM #(.addrWidth(14)) rom_1 (.addr({counter_2_q_2, counter_2_q, counter_1_q[7:2]}));  // open: data, sel
  nand nand_1 (nand_1_out, counter_1_q[0], counter_1_q[1]);
  and and_1 (and_1_out, nand_1_out, in_1);
  not not_3 (not_3_out, in_3[2]);
  Decoder #(.select(2), .disabled(0)) decoder_1 (
    .out0(decoder_1_out0), .out1(decoder_1_out1), .out2(decoder_1_out2), .out3(decoder_1_out3),
    .sel(in_3[1:0]), .en(in_3[2]));
  Clock clock_1 (.out(clock_1_out));
endmodule

// 189
module _74ls189 (
  input  [3:0] Data,
  input  Clear,
  input  WE,
  input  [3:0] Address,
  input  CS,
  output [3:0] out_6
);

  wire decoder_1_out0, decoder_1_out1, decoder_1_out2, decoder_1_out3, decoder_1_out4, decoder_1_out5,
       decoder_1_out6, decoder_1_out7, decoder_1_out8, decoder_1_out9, decoder_1_out10, decoder_1_out11,
       decoder_1_out12, decoder_1_out13, decoder_1_out14, decoder_1_out15, not_1_out, not_2_out;
  wire [3:0] register_1_q, register_2_q, register_3_q, register_4_q, register_5_q, register_6_q,
       register_7_q, register_8_q, register_9_q, register_10_q, register_11_q, register_12_q, register_13_q,
       register_14_q, register_15_q, register_16_q;

  not not_1 (not_1_out, CS);
  not not_2 (not_2_out, Clear);
  assign out_6 = decoder_1_out0 ? register_1_q : 4'bz;  // Controlled_Buffer controlled_buffer_1
  Register #(.width(4), .trigger("low")) register_1 (
    .D(Data), .en(decoder_1_out0), .Q(register_1_q), .clk(WE), .clr(not_2_out));
  Register #(.width(4), .trigger("low")) register_2 (
    .D(Data), .en(decoder_1_out1), .Q(register_2_q), .clk(WE), .clr(not_2_out));
  assign out_6 = decoder_1_out1 ? register_2_q : 4'bz;  // Controlled_Buffer controlled_buffer_2
  assign out_6 = decoder_1_out2 ? register_3_q : 4'bz;  // Controlled_Buffer controlled_buffer_3
  Register #(.width(4), .trigger("low")) register_3 (
    .D(Data), .en(decoder_1_out2), .Q(register_3_q), .clk(WE), .clr(not_2_out));
  assign out_6 = decoder_1_out3 ? register_4_q : 4'bz;  // Controlled_Buffer controlled_buffer_4
  Register #(.width(4), .trigger("low")) register_4 (
    .D(Data), .en(decoder_1_out3), .Q(register_4_q), .clk(WE), .clr(not_2_out));
  Register #(.width(4), .trigger("low")) register_5 (
    .D(Data), .en(decoder_1_out4), .Q(register_5_q), .clk(WE), .clr(not_2_out));
  assign out_6 = decoder_1_out4 ? register_5_q : 4'bz;  // Controlled_Buffer controlled_buffer_5
  assign out_6 = decoder_1_out5 ? register_6_q : 4'bz;  // Controlled_Buffer controlled_buffer_6
  Register #(.width(4), .trigger("low")) register_6 (
    .D(Data), .en(decoder_1_out5), .Q(register_6_q), .clk(WE), .clr(not_2_out));
  assign out_6 = decoder_1_out6 ? register_7_q : 4'bz;  // Controlled_Buffer controlled_buffer_7
  Register #(.width(4), .trigger("low")) register_7 (
    .D(Data), .en(decoder_1_out6), .Q(register_7_q), .clk(WE), .clr(not_2_out));
  Register #(.width(4), .trigger("low")) register_8 (
    .D(Data), .en(decoder_1_out7), .Q(register_8_q), .clk(WE), .clr(not_2_out));
  assign out_6 = decoder_1_out7 ? register_8_q : 4'bz;  // Controlled_Buffer controlled_buffer_8
  Decoder #(.select(4), .disabled(0)) decoder_1 (
    .out0(decoder_1_out0), .out1(decoder_1_out1), .out2(decoder_1_out2), .out3(decoder_1_out3),
    .out4(decoder_1_out4), .out5(decoder_1_out5), .out6(decoder_1_out6), .out7(decoder_1_out7),
    .out8(decoder_1_out8), .out9(decoder_1_out9), .out10(decoder_1_out10), .out11(decoder_1_out11),
    .out12(decoder_1_out12), .out13(decoder_1_out13), .out14(decoder_1_out14), .out15(decoder_1_out15),
    .sel(Address), .en(not_1_out));
  Register #(.width(4), .trigger("low")) register_9 (
    .D(Data), .en(decoder_1_out8), .Q(register_9_q), .clk(WE), .clr(not_2_out));
  assign out_6 = decoder_1_out8 ? register_9_q : 4'bz;  // Controlled_Buffer controlled_buffer_9
  Register #(.width(4), .trigger("low")) register_10 (
    .D(Data), .en(decoder_1_out9), .Q(register_10_q), .clk(WE), .clr(not_2_out));
  assign out_6 = decoder_1_out9 ? register_10_q : 4'bz;  // Controlled_Buffer controlled_buffer_10
  Register #(.width(4), .trigger("low")) register_11 (
    .D(Data), .en(decoder_1_out10), .Q(register_11_q), .clk(WE), .clr(not_2_out));
  assign out_6 = decoder_1_out10 ? register_11_q : 4'bz;  // Controlled_Buffer controlled_buffer_11
  Register #(.width(4), .trigger("low")) register_12 (
    .D(Data), .en(decoder_1_out11), .Q(register_12_q), .clk(WE), .clr(not_2_out));
  assign out_6 = decoder_1_out11 ? register_12_q : 4'bz;  // Controlled_Buffer controlled_buffer_12
  assign out_6 = decoder_1_out12 ? register_13_q : 4'bz;  // Controlled_Buffer controlled_buffer_13
  Register #(.width(4), .trigger("low")) register_13 (
    .D(Data), .en(decoder_1_out12), .Q(register_13_q), .clk(WE), .clr(not_2_out));
  Register #(.width(4), .trigger("low")) register_14 (
    .D(Data), .en(decoder_1_out13), .Q(register_14_q), .clk(WE), .clr(not_2_out));
  assign out_6 = decoder_1_out13 ? register_14_q : 4'bz;  // Controlled_Buffer controlled_buffer_14
  Register #(.width(4), .trigger("low")) register_15 (
    .D(Data), .en(decoder_1_out14), .Q(register_15_q), .clk(WE), .clr(not_2_out));
  assign out_6 = decoder_1_out14 ? register_15_q : 4'bz;  // Controlled_Buffer controlled_buffer_15
  assign out_6 = decoder_1_out15 ? register_16_q : 4'bz;  // Controlled_Buffer controlled_buffer_16
  Register #(.width(4), .trigger("low")) register_16 (
    .D(Data), .en(decoder_1_out15), .Q(register_16_q), .clk(WE), .clr(not_2_out));
endmodule

module processor_idea_2 (
  input  Clear__minor,
  input  in_2,
  output [3:0] out_3,
  output [3:0] out_4,
  output [3:0] out_5,
  output [3:0] out_6,
  output [7:0] RAM_BYTE,
  output [3:0] ALU_RESULT,
  output [3:0] out_9,
  output [3:0] out_10,
  output [3:0] out_11,
  output [3:0] out_12,
  output [3:0] out_13,
  output [3:0] out_14,
  output [3:0] out_15,
  output [3:0] out_16,
  output [3:0] Address,
  output [3:0] ALU_Operand_A,
  output [3:0] ALU_Operand_B
);

  wire and_1_out, and_2_out, clock_1_out, decoder_1_out0, decoder_1_out1, decoder_1_out2, decoder_1_out3,
       decoder_1_out4, decoder_1_out5, decoder_1_out6, decoder_1_out7, n74ls161_1_rco, n74ls161_3_rco,
       n74ls161_4_rco, n74ls195_1_nq3, n74ls195_2_nq3, n74ls195_3_nq3, n74ls195_4_nq3, n74ls195_5_nq3,
       n74ls195_6_nq3, not_1_out, not_2_out, not_3_out, not_4_out, not_5_out, not_6_out, not_7_out,
       not_8_out, not_9_out, not_10_out, not_11_out, not_12_out, not_13_out, not_14_out, not_15_out,
       not_16_out, not_17_out, or_1_out, or_2_out, or_3_out, or_4_out;
  wire [2:0] n74ls161_3_data_out, rom_1_data_2;
  wire [7:0] rom_1_data;
  wire [12:0] n74ls161_3_data_out_2;

  or or_1 (or_1_out, clock_1_out, not_14_out);
  _74ls195 u_74ls195_1 (
    .Clock(or_1_out), .clear(Clear__minor), .Parallel_In(ALU_RESULT), .J(not_10_out),
    .Parallel_Load(not_14_out), .Parallel_Out(out_11), .nQ3(n74ls195_1_nq3));
  not not_1 (not_1_out, n74ls195_1_nq3);
  or or_2 (or_2_out, clock_1_out, not_13_out);
  not not_2 (not_2_out, and_1_out);
  not not_3 (not_3_out, Clear__minor);
  and and_1 (and_1_out, not_13_out, not_16_out);
  and and_2 (and_2_out, not_4_out, not_16_out);
  not not_4 (not_4_out, not_13_out);
  _74ls195 u_74ls195_2 (
    .Clock(or_2_out), .clear(Clear__minor), .Parallel_In(RAM_BYTE[7:4]), .J(not_1_out),
    .Parallel_Load(not_13_out), .Parallel_Out(out_12), .nQ3(n74ls195_2_nq3));
  not not_5 (not_5_out, not_16_out);
  assign RAM_BYTE = not_5_out ? {out_12, out_13} : 8'bz;  // Controlled_Buffer controlled_buffer_1
  RAM #(.addrWidth(12), .bus("asynch")) ram_1 (
    .addr({out_11, out_14, ALU_Operand_B}), .data(RAM_BYTE), .sel(not_2_out), .ld(and_2_out), .clr(not_3_out));
  not not_6 (not_6_out, n74ls195_2_nq3);
  Clock clock_1 (.out(clock_1_out));
  _74ls195 u_74ls195_3 (
    .Clock(or_2_out), .clear(Clear__minor), .Parallel_In(RAM_BYTE[3:0]), .J(not_6_out),
    .Parallel_Load(not_13_out), .Parallel_Out(out_13), .nQ3(n74ls195_3_nq3));
  not not_7 (not_7_out, n74ls195_3_nq3);
  or or_3 (or_3_out, clock_1_out, not_12_out);
  _74ls161 u_74ls161_1 (
    .Data_In(ALU_RESULT), .Count_Enable(n74ls161_3_rco), .nLoad(not_15_out), .Clock(clock_1_out),
    .nClear(Clear__minor), .Data_Out(n74ls161_3_data_out_2[4:1]), .RCO(n74ls161_1_rco), .Data_Out_2(out_5));
  _74ls161 u_74ls161_2 (
    .Data_In(out_5), .Count_Enable(n74ls161_4_rco), .nLoad(not_15_out), .Clock(clock_1_out),
    .nClear(Clear__minor), .Data_Out(n74ls161_3_data_out_2[12:9]), .Data_Out_2(out_9));  // open: RCO
  _74ls195 u_74ls195_4 (
    .Clock(or_3_out), .clear(Clear__minor), .Parallel_In(out_9), .J(not_7_out), .Parallel_Load(not_12_out),
    .Parallel_Out(out_14), .nQ3(n74ls195_4_nq3));
  not not_8 (not_8_out, n74ls195_4_nq3);
  _74ls161 u_74ls161_3 (
    .Data_In(Address), .Count_Enable(not_15_out), .nLoad(not_15_out), .Clock(clock_1_out),
    .nClear(Clear__minor), .Data_Out({n74ls161_3_data_out_2[0], n74ls161_3_data_out}), .RCO(n74ls161_3_rco),
    .Data_Out_2(out_6));
  _74ls161 u_74ls161_4 (
    .Data_In(out_6), .Count_Enable(n74ls161_1_rco), .nLoad(not_15_out), .Clock(clock_1_out),
    .nClear(Clear__minor), .Data_Out(n74ls161_3_data_out_2[8:5]), .RCO(n74ls161_4_rco), .Data_Out_2(out_10));
  _74ls195 u_74ls195_5 (
    .Clock(or_3_out), .clear(Clear__minor), .Parallel_In(out_10), .J(not_8_out), .Parallel_Load(not_12_out),
    .Parallel_Out(ALU_Operand_B), .nQ3(n74ls195_5_nq3));
  not not_9 (not_9_out, n74ls195_5_nq3);
  or or_4 (or_4_out, clock_1_out, not_11_out);
  _74ls189 u_74ls189_1 (
    .Data(ALU_Operand_B), .WE(not_17_out), .Address(Address), .CS(1'b0), .out_6(ALU_Operand_A),
    .Clear(Clear__minor));
  _74ls195 u_74ls195_6 (
    .Clock(or_4_out), .clear(Clear__minor), .Parallel_In(rom_1_data[3:0]), .J(not_9_out),
    .Parallel_Load(not_11_out), .Parallel_Out(Address), .nQ3(n74ls195_6_nq3));
  Adder #(.width(4)) adder_1 (.a(ALU_Operand_A), .b(ALU_Operand_B), .out(ALU_RESULT), .cin(in_2));  // open: cout
  ROM #(.addrWidth(15)) rom_1 (
    .addr({n74ls161_3_data_out_2, n74ls161_3_data_out[2:1]}),
    .data({rom_1_data[7], rom_1_data_2, rom_1_data[3:0]}), .sel(1'b1));
  not not_10 (not_10_out, n74ls195_6_nq3);
  not not_11 (not_11_out, decoder_1_out0);
  not not_12 (not_12_out, decoder_1_out1);
  not not_13 (not_13_out, decoder_1_out2);
  not not_14 (not_14_out, decoder_1_out3);
  not not_15 (not_15_out, decoder_1_out4);
  not not_16 (not_16_out, decoder_1_out5);
  not not_17 (not_17_out, decoder_1_out6);
  // NOT_Gate not_18 has open pins: in=decoder_1_out7, out=open
  Decoder #(.select(3), .disabled(0), .enable("false")) decoder_1 (
    .out0(decoder_1_out0), .out1(decoder_1_out1), .out2(decoder_1_out2), .out3(decoder_1_out3),
    .out4(decoder_1_out4), .out5(decoder_1_out5), .out6(decoder_1_out6), .out7(decoder_1_out7),
    .sel(rom_1_data_2));

  assign out_3 = ALU_RESULT;
  assign out_4 = Address;
  assign out_15 = ALU_Operand_B;
  assign out_16 = Address;

  // Notes on the sheet:
  //   contents of rom_1 (hex, n*v repeats v):
  //   40 767*0 11
  //   Shift All Right
endmodule

// 161
module _74ls161 (
  input  [3:0] Data_In,
  input  Count_Enable,
  input  nLoad,
  input  Clock,
  input  nClear,
  output [3:0] Data_Out,
  output [3:0] Data_Out_2,
  output RCO
);

  wire not_1_out, not_2_out, or_1_out;
  wire [3:0] adder_1_out, multiplexer_1_out;

  not not_1 (not_1_out, nLoad);
  not not_2 (not_2_out, nClear);
  Multiplexer #(.width(4), .enable("false")) multiplexer_1 (
    .in0(adder_1_out), .in1(Data_In), .out(multiplexer_1_out), .sel(not_1_out));
  or or_1 (or_1_out, Count_Enable, not_1_out);
  Adder #(.width(4)) adder_1 (.a(Data_Out), .b(4'b0001), .out(adder_1_out), .cout(RCO));  // open: cin
  Register #(.width(4)) register_1 (.D(multiplexer_1_out), .en(or_1_out), .Q(Data_Out), .clk(Clock), .clr(not_2_out));

  assign Data_Out_2 = Data_Out;
endmodule

module processor_3 (
  input  Clear__minor,
  output [3:0] out_2,
  output [3:0] out_3,
  output [3:0] out_4,
  output [3:0] out_5,
  output [3:0] out_6,
  output [3:0] out_7,
  output [3:0] out_8,
  output [3:0] out_9,
  output [3:0] out_10,
  output [3:0] out_11,
  output [3:0] out_12,
  output [3:0] out_13
);

  wire ALU_OP1_nq3, ALU_OP2_nq3, ALU_OP3_nq3, and_1_out, and_2_out, clock_1_out, CONSTANT_nq3,
       n74ls161_1_rco, n74ls161_3_rco, n74ls161_4_rco, not_1_out, not_2_out, not_3_out, not_4_out, not_5_out,
       not_6_out, not_7_out, not_8_out, not_9_out, not_10_out, not_11_out, PC_MSB_LSH_nq3, PC_MSB_MSH_nq3,
       RAM_READ_LSH_nq3, RAM_READ_MSH_nq3;
  wire [3:0] alu_1_aout, alu_1_bout, alu_1_cout, multiplexer_1_out, n74ls161_1_data_out, n74ls161_2_data_out,
       n74ls161_3_data_out, n74ls161_4_data_out;
  wire [7:0] ram_1_data, rom_1_data;

  Clock clock_1 (.out(clock_1_out));
  _74ls195 ALU_OP1 (
    .Clock(clock_1_out), .clear(Clear__minor), .Parallel_In(alu_1_aout), .J(not_11_out),
    .Parallel_Load(rom_1_data[4]), .Parallel_Out(out_6), .nQ3(ALU_OP1_nq3));
  not not_1 (not_1_out, ALU_OP1_nq3);
  not not_2 (not_2_out, and_2_out);
  and and_1 (and_1_out, not_3_out, rom_1_data[4]);
  and and_2 (and_2_out, rom_1_data[6], rom_1_data[4]);
  not not_3 (not_3_out, rom_1_data[6]);
  _74ls195 ALU_OP2 (
    .Clock(clock_1_out), .clear(Clear__minor), .Parallel_In(alu_1_bout), .J(not_1_out),
    .Parallel_Load(rom_1_data[4]), .Parallel_Out(out_7), .nQ3(ALU_OP2_nq3));
  not not_4 (not_4_out, ALU_OP2_nq3);
  not not_5 (not_5_out, rom_1_data[4]);
  RAM #(.addrWidth(12), .bus("asynch")) ram_1 (
    .addr({out_6, out_7, multiplexer_1_out}), .data(ram_1_data), .sel(not_2_out), .ld(and_1_out),
    .clr(Clear__minor));
  assign ram_1_data = not_5_out ? {out_9, out_10} : 8'bz;  // Controlled_Buffer controlled_buffer_1
  _74ls195 ALU_OP3 (
    .Clock(clock_1_out), .clear(Clear__minor), .Parallel_In(alu_1_cout), .J(not_4_out),
    .Parallel_Load(rom_1_data[4]), .Parallel_Out(out_8), .nQ3(ALU_OP3_nq3));
  not not_6 (not_6_out, ALU_OP3_nq3);
  Multiplexer #(.width(4), .enable("false")) multiplexer_1 (
    .in0(out_8), .in1(rom_1_data[3:0]), .out(multiplexer_1_out), .sel(rom_1_data[7]));
  _74ls161 u_74ls161_1 (
    .Data_In(multiplexer_1_out), .Count_Enable(n74ls161_3_rco), .nLoad(rom_1_data[5]), .Clock(clock_1_out),
    .nClear(Clear__minor), .Data_Out(n74ls161_1_data_out), .RCO(n74ls161_1_rco), .Data_Out_2(out_2));
  _74ls161 u_74ls161_2 (
    .Data_In(out_2), .Count_Enable(n74ls161_4_rco), .nLoad(rom_1_data[5]), .Clock(clock_1_out),
    .nClear(Clear__minor), .Data_Out(n74ls161_2_data_out), .Data_Out_2(out_4));  // open: RCO
  _74ls195 PC_MSB_MSH (
    .Clock(clock_1_out), .clear(Clear__minor), .Parallel_In(out_4), .J(not_6_out),
    .Parallel_Load(rom_1_data[4]), .Parallel_Out(out_9), .nQ3(PC_MSB_MSH_nq3));
  not not_7 (not_7_out, PC_MSB_MSH_nq3);
  _74ls161 u_74ls161_3 (
    .Data_In(alu_1_cout), .Count_Enable(rom_1_data[5]), .nLoad(rom_1_data[5]), .Clock(clock_1_out),
    .nClear(Clear__minor), .Data_Out(n74ls161_3_data_out), .RCO(n74ls161_3_rco), .Data_Out_2(out_3));
  _74ls161 u_74ls161_4 (
    .Data_In(out_3), .Count_Enable(n74ls161_1_rco), .nLoad(rom_1_data[5]), .Clock(clock_1_out),
    .nClear(Clear__minor), .Data_Out(n74ls161_4_data_out), .RCO(n74ls161_4_rco), .Data_Out_2(out_5));
  _74ls195 PC_MSB_LSH (
    .Clock(clock_1_out), .clear(Clear__minor), .Parallel_In(out_5), .J(not_7_out),
    .Parallel_Load(rom_1_data[4]), .Parallel_Out(out_10), .nQ3(PC_MSB_LSH_nq3));
  not not_8 (not_8_out, PC_MSB_LSH_nq3);
  _74ls195 RAM_READ_MSH (
    .Clock(clock_1_out), .clear(Clear__minor), .Parallel_In(ram_1_data[7:4]), .J(not_8_out),
    .Parallel_Load(rom_1_data[4]), .Parallel_Out(out_11), .nQ3(RAM_READ_MSH_nq3));
  not not_9 (not_9_out, RAM_READ_MSH_nq3);
  ROM #(.addrWidth(15)) rom_1 (
    .addr({n74ls161_2_data_out, n74ls161_4_data_out, n74ls161_1_data_out, n74ls161_3_data_out[3:1]}),
    .data(rom_1_data), .sel(1'b1));
  _74ls195 RAM_READ_LSH (
    .Clock(clock_1_out), .clear(Clear__minor), .Parallel_In(ram_1_data[3:0]), .J(not_9_out),
    .Parallel_Load(rom_1_data[4]), .Parallel_Out(out_12), .nQ3(RAM_READ_LSH_nq3));
  not not_10 (not_10_out, RAM_READ_LSH_nq3);
  ALU alu_1 (.A(out_11), .B(out_12), .C(out_13), .AOUT(alu_1_aout), .BOUT(alu_1_bout), .COUT(alu_1_cout));
  _74ls195 CONSTANT (
    .Clock(clock_1_out), .clear(Clear__minor), .Parallel_In(rom_1_data[3:0]), .J(not_10_out),
    .Parallel_Load(rom_1_data[4]), .Parallel_Out(out_13), .nQ3(CONSTANT_nq3));
  not not_11 (not_11_out, CONSTANT_nq3);

  // Notes on the sheet:
  //   RAM ADDRESS
  //   RAM WRITE BYTE
  //   contents of rom_1 (hex, n*v repeats v):
  //   40 767*0 11
endmodule

module ALU (
  input  [3:0] A,
  input  [3:0] B,
  input  [3:0] C,
  output [3:0] AOUT,
  output [3:0] BOUT,
  output [3:0] COUT
);

  assign AOUT = ~(A & B);  // NAND_Gate nand_1, 4 bits wide
  Adder #(.width(4)) adder_1 (.a(B), .b(C), .out(BOUT));  // open: cin, cout
  assign COUT = ~C;  // NOT_Gate not_1, 4 bits wide
endmodule

module processor_4 (
  input  in_1,
  output [3:0] out_2,
  output [3:0] out_3,
  output [3:0] out_4,
  output [3:0] out_5,
  output [3:0] out_6,
  output [3:0] out_7,
  output [3:0] out_8,
  output [3:0] out_9,
  output [3:0] out_10,
  output [3:0] out_11
);

  wire ALU_OP1_nq3, ALU_OP2_nq3, and_1_out, and_2_out, and_3_out, clock_1_out, CONSTANT_nq3, decoder_1_out0,
       decoder_1_out1, decoder_1_out2, decoder_1_out3, decoder_1_out4, decoder_1_out5, decoder_1_out6,
       decoder_1_out7, n74ls161_1_rco, n74ls161_3_rco, n74ls161_4_rco, not_1_out, not_2_out, not_3_out,
       not_4_out, not_5_out, not_6_out, not_7_out, not_8_out, not_9_out, not_10_out, not_11_out, not_12_out,
       not_13_out, not_14_out, not_15_out, or_1_out, or_2_out, or_3_out, or_4_out, or_5_out, or_6_out,
       or_7_out, or_8_out, or_9_out, or_10_out, or_11_out, or_12_out, or_13_out, or_14_out, or_15_out,
       PC_MSB_LSH_nq3, PC_MSB_MSH_nq3, pull_resistor_1_node, pull_resistor_2_node, pull_resistor_4_node,
       pull_resistor_5_node, pull_resistor_6_node, pull_resistor_7_node, pull_resistor_8_node,
       RAM_READ_MSH_nq3;
  wire [3:0] alu_2_1_p3, alu_2_1_p4, n74ls161_1_data_out, n74ls161_2_data_out, n74ls161_3_data_out,
       n74ls161_4_data_out;
  wire [7:0] alu_2_1_p1, rom_1_data, undriven;

  Clock clock_1 (.out(clock_1_out));
  // ALU_2 alu_2_1: pin names not known; wires that end beside it: alu_2_1_p1[3:0], out_8, alu_2_1_p3, alu_2_1_p4
  _74ls195 ALU_OP1 (
    .Clock(or_2_out), .clear(in_1), .Parallel_In(alu_2_1_p3), .J(not_9_out), .Parallel_Load(or_1_out),
    .Parallel_Out(out_6), .nQ3(ALU_OP1_nq3));
  or or_1 (or_1_out, pull_resistor_4_node, rom_1_data[7]);
  or or_2 (or_2_out, clock_1_out, pull_resistor_4_node);
  not not_1 (not_1_out, and_2_out);
  and and_1 (and_1_out, not_2_out, or_5_out);
  and and_2 (and_2_out, or_6_out, or_5_out);
  not not_2 (not_2_out, or_6_out);
  not not_3 (not_3_out, ALU_OP1_nq3);
  or or_3 (or_3_out, pull_resistor_5_node, rom_1_data[7]);
  or or_4 (or_4_out, clock_1_out, pull_resistor_5_node);
  not not_4 (not_4_out, or_5_out);
  assign alu_2_1_p1 = not_4_out ? {out_9, out_10} : 8'bz;  // Controlled_Buffer controlled_buffer_1
  RAM #(.addrWidth(16), .bus("asynch")) ram_1 (
    .addr({out_6, out_7, out_8, rom_1_data[3:0]}), .data(alu_2_1_p1), .sel(not_1_out), .ld(and_1_out));  // open: clr
  or or_5 (or_5_out, pull_resistor_1_node, rom_1_data[6]);
  or or_6 (or_6_out, pull_resistor_2_node, rom_1_data[6]);
  _74ls195 ALU_OP2 (
    .Clock(or_4_out), .clear(in_1), .Parallel_In(alu_2_1_p4), .J(not_3_out), .Parallel_Load(or_3_out),
    .Parallel_Out(out_7), .nQ3(ALU_OP2_nq3));
  not not_5 (not_5_out, ALU_OP2_nq3);
  assign alu_2_1_p1 = rom_1_data[6] ? undriven : 8'bz;  // Controlled_Buffer controlled_buffer_2
  Pull_Resistor #(.pull(1)) pull_resistor_1 (.node(pull_resistor_1_node));
  Pull_Resistor #(.pull(1)) pull_resistor_2 (.node(pull_resistor_2_node));
  Pull_Resistor #(.pull(1)) pull_resistor_3 (.node(rom_1_data[6]));
  _74ls195 CONSTANT (
    .Clock(or_8_out), .clear(in_1), .Parallel_In(rom_1_data[3:0]), .J(not_5_out), .Parallel_Load(or_7_out),
    .Parallel_Out(out_8), .nQ3(CONSTANT_nq3));
  or or_7 (or_7_out, pull_resistor_7_node, rom_1_data[7]);
  or or_8 (or_8_out, clock_1_out, pull_resistor_7_node);
  not not_6 (not_6_out, CONSTANT_nq3);
  or or_9 (or_9_out, pull_resistor_6_node, rom_1_data[7]);
  or or_10 (or_10_out, clock_1_out, pull_resistor_6_node);
  _74ls161 u_74ls161_1 (
    .Data_In(alu_2_1_p1[7:4]), .Count_Enable(n74ls161_3_rco), .nLoad(pull_resistor_8_node),
    .Clock(clock_1_out), .nClear(in_1), .Data_Out(n74ls161_1_data_out), .RCO(n74ls161_1_rco),
    .Data_Out_2(out_2));
  _74ls161 u_74ls161_2 (
    .Data_In(out_2), .Count_Enable(n74ls161_4_rco), .nLoad(pull_resistor_8_node), .Clock(clock_1_out),
    .nClear(in_1), .Data_Out(n74ls161_2_data_out), .Data_Out_2(out_4));  // open: RCO
  _74ls195 PC_MSB_MSH (
    .Clock(or_10_out), .clear(in_1), .Parallel_In(out_4), .J(not_6_out), .Parallel_Load(or_9_out),
    .Parallel_Out(out_9), .nQ3(PC_MSB_MSH_nq3));
  not not_7 (not_7_out, PC_MSB_MSH_nq3);
  _74ls161 u_74ls161_3 (
    .Data_In(alu_2_1_p3), .Count_Enable(pull_resistor_8_node), .nLoad(pull_resistor_8_node),
    .Clock(clock_1_out), .nClear(in_1), .Data_Out(n74ls161_3_data_out), .RCO(n74ls161_3_rco),
    .Data_Out_2(out_3));
  _74ls161 u_74ls161_4 (
    .Data_In(out_3), .Count_Enable(n74ls161_1_rco), .nLoad(pull_resistor_8_node), .Clock(clock_1_out),
    .nClear(in_1), .Data_Out(n74ls161_4_data_out), .RCO(n74ls161_4_rco), .Data_Out_2(out_5));
  _74ls195 PC_MSB_LSH (
    .Clock(or_12_out), .clear(in_1), .Parallel_In(out_5), .J(not_7_out), .Parallel_Load(or_11_out),
    .Parallel_Out(out_10), .nQ3(PC_MSB_LSH_nq3));
  or or_11 (or_11_out, pull_resistor_6_node, rom_1_data[7]);
  or or_12 (or_12_out, clock_1_out, pull_resistor_6_node);
  not not_8 (not_8_out, PC_MSB_LSH_nq3);
  or or_13 (or_13_out, and_3_out, rom_1_data[7]);
  or or_14 (or_14_out, clock_1_out, and_3_out);
  and and_3 (and_3_out, pull_resistor_4_node, pull_resistor_5_node);
  _74ls195 RAM_READ_MSH (
    .Clock(or_14_out), .clear(in_1), .Parallel_In(alu_2_1_p1[7:4]), .J(not_8_out), .Parallel_Load(or_13_out),
    .Parallel_Out(out_11), .nQ3(RAM_READ_MSH_nq3));
  not not_9 (not_9_out, RAM_READ_MSH_nq3);
  Pull_Resistor pull_resistor_4 (.node(pull_resistor_4_node));
  Controlled_Buffer controlled_buffer_3 ();  // open: in, out, en
  ROM #(.addrWidth(15)) rom_1 (
    .addr({n74ls161_2_data_out, n74ls161_4_data_out, n74ls161_1_data_out, n74ls161_3_data_out[3:1]}),
    .data(rom_1_data), .sel(1'b1));
  Pull_Resistor pull_resistor_5 (.node(pull_resistor_5_node));
  Pull_Resistor pull_resistor_6 (.node(pull_resistor_6_node));
  Pull_Resistor pull_resistor_7 (.node(pull_resistor_7_node));
  Pull_Resistor #(.pull(1)) pull_resistor_8 (.node(pull_resistor_8_node));
  and and_4 (pull_resistor_2_node, ~rom_1_data[6], rom_1_data[5], rom_1_data[4]);  // AND_Gate
  Decoder #(.select(3), .disabled(0)) decoder_1 (
    .out0(decoder_1_out0), .out1(decoder_1_out1), .out2(decoder_1_out2), .out3(decoder_1_out3),
    .out4(decoder_1_out4), .out5(decoder_1_out5), .out6(decoder_1_out6), .out7(decoder_1_out7),
    .sel(rom_1_data[6:4]), .en(rom_1_data[7]));
  not not_10 (not_10_out, decoder_1_out3);
  not not_11 (not_11_out, decoder_1_out0);
  not not_12 (not_12_out, decoder_1_out5);
  not not_13 (not_13_out, decoder_1_out2);
  not not_14 (not_14_out, decoder_1_out4);
  not not_15 (not_15_out, decoder_1_out1);
  // NOT_Gate not_16 has open pins: in=decoder_1_out6, out=open
  assign pull_resistor_5_node = or_15_out ? not_15_out : 1'bz;  // Controlled_Buffer controlled_buffer_4
  assign pull_resistor_4_node = or_15_out ? not_11_out : 1'bz;  // Controlled_Buffer controlled_buffer_5
  assign pull_resistor_8_node = or_15_out ? not_13_out : 1'bz;  // Controlled_Buffer controlled_buffer_6
  assign pull_resistor_1_node = or_15_out ? not_10_out : 1'bz;  // Controlled_Buffer controlled_buffer_7
  assign pull_resistor_7_node = or_15_out ? not_12_out : 1'bz;  // Controlled_Buffer controlled_buffer_8
  assign pull_resistor_6_node = or_15_out ? not_14_out : 1'bz;  // Controlled_Buffer controlled_buffer_9
  or or_15 (or_15_out, n74ls161_3_data_out[0], rom_1_data[7]);
  // NOT_Gate not_17 has open pins: in=decoder_1_out7, out=open
  Pull_Resistor pull_resistor_9 (.node(or_15_out));

  // Notes on the sheet:
  //   RAM ADDRESS
  //   RAM WRITE BYTE
  //   RAM READ BYTE
  //   contents of rom_1 (hex, n*v repeats v):
  //   51 80 766*0 11
endmodule

// ALU
module ALU_2 (
  input  [3:0] A,
  input  [3:0] B,
  output [3:0] OP1,
  output nop_eq_0,
  output [3:0] OP2,
  output cout
);

  Pull_Resistor pull_resistor_1 (.node(A));
  Pull_Resistor pull_resistor_2 (.node(B));
  assign OP1 = ~(A & B);  // NAND_Gate nand_1, 4 bits wide
  Adder #(.width(4)) adder_1 (.a(B), .b(A), .out(OP2), .cout(cout));  // open: cin
  or or_1 (nop_eq_0, OP2[0], OP2[1], OP2[2], OP2[3]);
endmodule

module processor_5 (
  input  in_1,
  output [3:0] out_2,
  output [3:0] out_3,
  output [3:0] out_4,
  output [3:0] out_5,
  output [3:0] out_6,
  output [3:0] out_7,
  output [3:0] out_8,
  output [3:0] out_9,
  output [3:0] out_10,
  output [3:0] out_11
);

  wire alu_2_1_cout, alu_2_1_nop_eq_0, ALU_OP1_nq3, ALU_OP2_nq3, and_1_out, and_2_out, and_3_out, and_4_out,
       clock_1_out, CONSTANT_nq3, controlled_buffer_2_out, decoder_1_out0, decoder_1_out1, decoder_1_out2,
       decoder_1_out3, decoder_1_out4, decoder_1_out5, decoder_1_out6, decoder_1_out7, decoder_2_out0,
       decoder_2_out1, decoder_2_out2, decoder_2_out3, decoder_2_out4, decoder_2_out5, decoder_2_out6,
       decoder_2_out7, n74ls161_1_rco, n74ls161_3_rco, n74ls161_4_rco, not_1_out, not_2_out, not_3_out,
       not_4_out, not_5_out, not_6_out, not_7_out, not_8_out, not_9_out, not_10_out, not_11_out, not_12_out,
       not_14_out, not_15_out, not_17_out, not_18_out, not_20_out, not_21_out, not_22_out, not_23_out,
       not_24_out, not_25_out, not_26_out, not_27_out, ONESH_TWOSH_out, or_1_out, or_2_out, or_3_out,
       PC_MSB_LSH_nq3, PC_MSB_MSH_nq3, pull_resistor_1_node, pull_resistor_3_node, pull_resistor_4_node,
       pull_resistor_5_node, RAM_CS_out, RAM_READ_MSH_nq3, SHIFT_ALL_out, WriteSRPulse_out;
  wire [3:0] alu_2_1_op1, alu_2_1_op2, n74ls161_1_data_out, n74ls161_2_data_out, n74ls161_3_data_out,
       n74ls161_4_data_out;
  wire [7:0] controlled_buffer_1_out, rom_1_data;

  Clock clock_1 (.out(clock_1_out));
  ALU_2 alu_2_1 (
    .A(controlled_buffer_1_out[3:0]), .B(out_11), .OP1(alu_2_1_op1), .nop_eq_0(alu_2_1_nop_eq_0),
    .OP2(alu_2_1_op2), .cout(alu_2_1_cout));
  _74ls195 ALU_OP1 (
    .Clock(controlled_buffer_2_out), .clear(in_1), .Parallel_In(alu_2_1_op1), .J(not_10_out),
    .Parallel_Load(not_15_out), .Parallel_Out(out_6), .nQ3(ALU_OP1_nq3));
  not not_1 (not_1_out, in_1);
  not not_2 (not_2_out, rom_1_data[6]);
  not not_3 (not_3_out, RAM_CS_out);
  not not_4 (not_4_out, ALU_OP1_nq3);
  not not_5 (not_5_out, not_3_out);
  assign controlled_buffer_1_out = not_5_out ? {out_9, out_10} : 8'bz;  // Controlled_Buffer controlled_buffer_1
  RAM #(.addrWidth(16), .bus("asynch")) ram_1 (
    .addr({out_6, out_7, out_8, rom_1_data[3:0]}), .data(controlled_buffer_1_out), .sel(not_2_out),
    .ld(not_3_out), .clr(not_1_out));
  _74ls195 ALU_OP2 (
    .Clock(pull_resistor_3_node), .clear(in_1), .Parallel_In(alu_2_1_op2), .J(not_4_out),
    .Parallel_Load(not_12_out), .Parallel_Out(out_7), .nQ3(ALU_OP2_nq3));
  not not_6 (not_6_out, ALU_OP2_nq3);
  _74ls195 CONSTANT (
    .Clock(pull_resistor_5_node), .clear(in_1), .Parallel_In(rom_1_data[3:0]), .J(not_6_out),
    .Parallel_Load(not_11_out), .Parallel_Out(out_8), .nQ3(CONSTANT_nq3));
  not not_7 (not_7_out, CONSTANT_nq3);
  _74ls161 u_74ls161_1 (
    .Data_In(controlled_buffer_1_out[7:4]), .Count_Enable(n74ls161_3_rco), .nLoad(pull_resistor_1_node),
    .Clock(clock_1_out), .nClear(in_1), .Data_Out(n74ls161_1_data_out), .RCO(n74ls161_1_rco),
    .Data_Out_2(out_2));
  _74ls161 u_74ls161_2 (
    .Data_In(out_2), .Count_Enable(n74ls161_4_rco), .nLoad(pull_resistor_1_node), .Clock(clock_1_out),
    .nClear(in_1), .Data_Out(n74ls161_2_data_out), .Data_Out_2(out_4));  // open: RCO
  _74ls195 PC_MSB_MSH (
    .Clock(pull_resistor_4_node), .clear(in_1), .Parallel_In(out_4), .J(not_7_out),
    .Parallel_Load(not_17_out), .Parallel_Out(out_9), .nQ3(PC_MSB_MSH_nq3));
  not not_8 (not_8_out, PC_MSB_MSH_nq3);
  _74ls161 u_74ls161_3 (
    .Data_In(controlled_buffer_1_out[3:0]), .Count_Enable(pull_resistor_1_node),
    .nLoad(pull_resistor_1_node), .Clock(clock_1_out), .nClear(in_1), .Data_Out(n74ls161_3_data_out),
    .RCO(n74ls161_3_rco), .Data_Out_2(out_3));
  _74ls161 u_74ls161_4 (
    .Data_In(out_3), .Count_Enable(n74ls161_1_rco), .nLoad(pull_resistor_1_node), .Clock(clock_1_out),
    .nClear(in_1), .Data_Out(n74ls161_4_data_out), .RCO(n74ls161_4_rco), .Data_Out_2(out_5));
  _74ls195 PC_MSB_LSH (
    .Clock(pull_resistor_4_node), .clear(in_1), .Parallel_In(out_5), .J(not_8_out),
    .Parallel_Load(not_17_out), .Parallel_Out(out_10), .nQ3(PC_MSB_LSH_nq3));
  not not_9 (not_9_out, PC_MSB_LSH_nq3);
  and and_1 (and_1_out, controlled_buffer_2_out, pull_resistor_3_node);
  _74ls195 RAM_READ_MSH (
    .Clock(and_1_out), .clear(in_1), .Parallel_In(controlled_buffer_1_out[7:4]), .J(not_9_out),
    .Parallel_Load(and_2_out), .Parallel_Out(out_11), .nQ3(RAM_READ_MSH_nq3));
  not not_10 (not_10_out, RAM_READ_MSH_nq3);
  ROM #(.addrWidth(15)) rom_1 (
    .addr({n74ls161_2_data_out, n74ls161_4_data_out, n74ls161_1_data_out, n74ls161_3_data_out[3:1]}),
    .data(rom_1_data), .sel(1'b1));
  and and_2 (and_2_out, not_15_out, not_12_out);
  Pull_Resistor #(.pull(1)) pull_resistor_1 (.node(pull_resistor_1_node));
  and RAM_CS (RAM_CS_out, ~rom_1_data[6], rom_1_data[5], rom_1_data[4]);  // AND_Gate
  and ONESH_TWOSH (ONESH_TWOSH_out, rom_1_data[6], n74ls161_3_data_out[0]);
  Decoder #(.select(3), .disabled(0)) decoder_1 (
    .out0(decoder_1_out0), .out1(decoder_1_out1), .out2(decoder_1_out2), .out3(decoder_1_out3),
    .out4(decoder_1_out4), .out5(decoder_1_out5), .out6(decoder_1_out6), .out7(decoder_1_out7),
    .sel(rom_1_data[6:4]), .en(rom_1_data[7]));
  not not_11 (not_11_out, decoder_1_out5);
  not not_12 (not_12_out, decoder_1_out1);
  not not_13 (pull_resistor_1_node, decoder_1_out2);
  not not_14 (not_14_out, decoder_1_out3);
  not not_15 (not_15_out, decoder_1_out0);
  // NOT_Gate not_16 has open pins: in=decoder_1_out6, out=open
  not not_17 (not_17_out, decoder_1_out4);
  and WriteSRPulse (WriteSRPulse_out, clock_1_out, n74ls161_3_data_out[0], rom_1_data[7]);
  Decoder #(.select(3), .disabled(0)) decoder_2 (
    .out0(decoder_2_out0), .out1(decoder_2_out1), .out2(decoder_2_out2), .out3(decoder_2_out3),
    .out4(decoder_2_out4), .out5(decoder_2_out5), .out6(decoder_2_out6), .out7(decoder_2_out7),
    .sel(rom_1_data[6:4]), .en(WriteSRPulse_out));
  not not_18 (not_18_out, decoder_2_out0);
  // NOT_Gate not_19 has open pins: in=decoder_1_out7, out=open
  assign controlled_buffer_2_out = or_3_out ? not_18_out : 1'bz;  // Controlled_Buffer controlled_buffer_2
  Pull_Resistor pull_resistor_2 (.node(controlled_buffer_2_out));
  Pull_Resistor pull_resistor_3 (.node(pull_resistor_3_node));
  Pull_Resistor pull_resistor_4 (.node(pull_resistor_4_node));
  Pull_Resistor pull_resistor_5 (.node(pull_resistor_5_node));
  and and_3 (and_3_out, rom_1_data[5], rom_1_data[4]);
  not not_20 (not_20_out, and_3_out);
  or or_1 (or_1_out, rom_1_data[4], alu_2_1_nop_eq_0);
  or or_2 (or_2_out, rom_1_data[5], alu_2_1_cout);
  or SHIFT_ALL (SHIFT_ALL_out, rom_1_data[7], ONESH_TWOSH_out, clock_1_out);
  not not_21 (not_21_out, decoder_2_out6);
  not not_22 (not_22_out, decoder_2_out1);
  not not_23 (not_23_out, decoder_2_out3);
  not not_24 (not_24_out, decoder_2_out2);
  not not_25 (not_25_out, decoder_2_out4);
  not not_26 (not_26_out, decoder_2_out7);
  not not_27 (not_27_out, decoder_2_out5);
  assign pull_resistor_3_node = or_3_out ? not_22_out : 1'bz;  // Controlled_Buffer controlled_buffer_3
  Controlled_Buffer controlled_buffer_4 (.in(not_24_out), .en(or_3_out));  // open: out
  Controlled_Buffer controlled_buffer_5 (.in(not_23_out), .en(or_3_out));  // open: out
  Controlled_Buffer controlled_buffer_6 (.in(not_26_out), .en(or_3_out));  // open: out
  assign pull_resistor_4_node = or_3_out ? not_25_out : 1'bz;  // Controlled_Buffer controlled_buffer_7
  assign pull_resistor_5_node = or_3_out ? not_27_out : 1'bz;  // Controlled_Buffer controlled_buffer_8
  Controlled_Buffer controlled_buffer_9 (.in(not_21_out), .en(or_3_out));  // open: out
  and and_4 (and_4_out, not_20_out, or_1_out, or_2_out);
  or or_3 (or_3_out, and_4_out, SHIFT_ALL_out);
  Pull_Resistor pull_resistor_6 (.node(or_3_out));

  // Notes on the sheet:
  //   RAM ADDRESS
  //   RAM WRITE BYTE
  //   RAM READ BYTE
  //   contents of rom_1 (hex, n*v repeats v):
  //   d1 a0 10 d1 f0 0 b0 d0 0 10 20 30 40 40 50 60 70 80 90 a0 b2 107*0 a0 127*0 a0 127*0 a0 127*0 a0
  //   127*0 a0 127*0 a0 127*0 a0 127*0 a0 127*0 a0 127*0 a0 127*0 a0 127*0 a0 127*0 a0 127*0 a0 127*0 a0
  //   127*0 a0 127*0 a0 127*0 a0 127*0 a0 127*0 a0 127*0 a0 127*0 a0 127*0 a0 127*0 a0 127*0 a0 127*0 a0
  //   127*0 a0 127*0 a0 127*0 a0 127*0 a0 127*0 a0 127*0 a0 127*0 a0 127*0 a0 127*0 a0 127*0 a0 127*0 a0
  //   127*0 a0 127*0 a0 127*0 a0 127*0 a0 127*0 a0 127*0 a0 127*0 a0 127*0 a0 127*0 a0 127*0 a0 127*0 a0
  //   127*0 a0 127*0 a0 127*0 a0 127*0 a0 127*0 a0 127*0 a0 127*0 a0 127*0 a0 127*0 a0 127*0 a0 127*0 a0
  //   127*0 a0 127*0 a0 127*0 a0 127*0 a0 127*0 a0 127*0 a0 127*0 a0 127*0 a0 127*0 a0 127*0 a0 127*0 a0
  //   127*0 a0 127*0 a0 127*0 a0 127*0 a0 127*0 a0 127*0 a0 127*0 a0 127*0 a0 127*0 a0 127*0 a0 127*0 a0
  //   127*0 a0 127*0 a0 127*0 a0 127*0 a0 127*0 a0 127*0 a0 127*0 a0 127*0 a0 127*0 a0 127*0 a0 127*0 a0
  //   127*0 a0 127*0 a0 127*0 a0 127*0 a0 127*0 a0 127*0 a0 127*0 a0 127*0 a0 127*0 a0 127*0 a0 127*0 a0
  //   127*0 a0 127*0 a0 127*0 a0 127*0 a0 127*0 a0 127*0 a0 127*0 a0 127*0 a0 127*0 a0 127*0 a0 127*0 a0
  //   127*0 a0 127*0 a0 127*0 a0 127*0 a0 127*0 a0 127*0 a0 127*0 a0 127*0 a0 127*0 a0 127*0 a0 127*0 a0
  //   127*0 a0 127*0 a0 127*0 a0 127*0 a0 127*0 a0 127*0 a0 127*0 a0 127*0 a0 127*0 a0 127*0 a0 127*0 a0
  //   127*0 a0 127*0 a0 127*0 a0 127*0 a0 127*0 a0 127*0 a0 127*0 a0 127*0 a0 127*0 a0 127*0 a0 127*0 a0
  //   127*0 a0 127*0 a0 127*0 a0 127*0 a0 127*0 a0 127*0 a0 127*0 a0 127*0 a0 127*0 a0 127*0 a0 127*0 a0
  //   127*0 a0 127*0 a0 127*0 a0 127*0 a0 127*0 a0 127*0 a0 127*0 a0 127*0 a0 127*0 a0 127*0 a0 127*0 a0
  //   127*0 a0 127*0 a0 127*0 a0 127*0 a0 127*0 a0 127*0 a0 127*0 a0 127*0 a0 127*0 a0 127*0 a0 127*0 a0
  //   127*0 a0 127*0 a0 127*0 a0 127*0 a0 127*0 a0 127*0 a0 127*0 a0 127*0 a0 127*0 a0 127*0 a0 127*0 a0
  //   127*0 a0 127*0 a0 127*0 a0 127*0 a0 127*0 a0 127*0 a0 127*0 a0 127*0 a0 127*0 a0 127*0 a0 127*0 a0
  //   127*0 a0 127*0 a0 127*0 a0 127*0 a0 127*0 a0 127*0 a0 127*0 a0 127*0 a0 127*0 a0 127*0 a0 127*0 a0
  //   127*0 a0 127*0 a0 127*0 a0 127*0 a0 127*0 a0 127*0 a0 127*0 a0 127*0 a0 127*0 a0 127*0 a0 127*0 a0
  //   127*0 a0 127*0 a0 127*0 a0 127*0 a0 127*0 a0 127*0 a0 127*0 a0 127*0 a0 127*0 a0 127*0 a0 127*0 a0
  //   127*0 a0 127*0 a0 127*0 a0 127*0 a0 127*0 a0 127*0 a0 127*0 a0 127*0 a0 127*0 a0 127*0 a0 127*0 a0
  //   127*0 a0 127*0 a0 127*0 a0 127*0 a0 127*0 a0 127*0 a0 127*0 a0 127*0 a0 127*0 a0
endmodule

// 4014
module hef4014bp (
  input  [7:0] Data_In,
  input  Parallel_Enable,
  input  Serial_In,
  input  Clock,
  output Q5,
  output Q6,
  output Q7
);

  wire and_1_out, and_2_out, and_3_out, and_4_out, and_5_out, and_6_out, and_7_out, and_8_out, and_9_out,
       and_10_out, and_11_out, and_12_out, and_13_out, and_14_out, and_15_out, and_16_out, d_ff_1_q,
       d_ff_2_q, d_ff_3_q, d_ff_4_q, d_ff_5_q, not_1_out, not_2_out, or_1_out, or_2_out, or_3_out, or_4_out,
       or_5_out, or_6_out, or_7_out, or_8_out;

  not not_1 (not_1_out, not_2_out);
  not not_2 (not_2_out, Parallel_Enable);
  and and_1 (and_1_out, Serial_In, not_2_out);
  or or_1 (or_1_out, and_1_out, and_2_out);
  and and_2 (and_2_out, not_1_out, Data_In[0]);
  D_Flip_Flop d_ff_1 (.clk(Clock), .D(or_1_out), .Q(d_ff_1_q));  // open: Qn, preset, en, reset
  and and_3 (and_3_out, d_ff_1_q, not_2_out);
  and and_4 (and_4_out, not_1_out, Data_In[1]);
  or or_2 (or_2_out, and_3_out, and_4_out);
  D_Flip_Flop d_ff_2 (.clk(Clock), .D(or_2_out), .Q(d_ff_2_q));  // open: Qn, preset, en, reset
  and and_5 (and_5_out, d_ff_2_q, not_2_out);
  and and_6 (and_6_out, not_1_out, Data_In[2]);
  or or_3 (or_3_out, and_5_out, and_6_out);
  and and_7 (and_7_out, d_ff_3_q, not_2_out);
  D_Flip_Flop d_ff_3 (.clk(Clock), .D(or_3_out), .Q(d_ff_3_q));  // open: Qn, preset, en, reset
  and and_8 (and_8_out, not_1_out, Data_In[3]);
  or or_4 (or_4_out, and_7_out, and_8_out);
  D_Flip_Flop d_ff_4 (.clk(Clock), .D(or_4_out), .Q(d_ff_4_q));  // open: Qn, preset, en, reset
  and and_9 (and_9_out, not_1_out, Data_In[4]);
  and and_10 (and_10_out, d_ff_4_q, not_2_out);
  or or_5 (or_5_out, and_10_out, and_9_out);
  and and_11 (and_11_out, d_ff_5_q, not_2_out);
  or or_6 (or_6_out, and_11_out, and_12_out);
  D_Flip_Flop d_ff_5 (.clk(Clock), .D(or_5_out), .Q(d_ff_5_q));  // open: Qn, preset, en, reset
  and and_12 (and_12_out, not_1_out, Data_In[5]);
  and and_13 (and_13_out, Q5, not_2_out);
  D_Flip_Flop d_ff_6 (.clk(Clock), .D(or_6_out), .Q(Q5));  // open: Qn, preset, en, reset
  and and_14 (and_14_out, not_1_out, Data_In[6]);
  or or_7 (or_7_out, and_13_out, and_14_out);
  D_Flip_Flop d_ff_7 (.clk(Clock), .D(or_7_out), .Q(Q6));  // open: Qn, preset, en, reset
  and and_15 (and_15_out, Q6, not_2_out);
  and and_16 (and_16_out, not_1_out, Data_In[7]);
  or or_8 (or_8_out, and_15_out, and_16_out);
  D_Flip_Flop d_ff_8 (.clk(Clock), .D(or_8_out), .Q(Q7));  // open: Qn, preset, en, reset
endmodule

module processor_6 (
  input  in_1,
  output [3:0] out_2,
  output [3:0] out_3,
  output [3:0] out_4,
  output [3:0] out_5
);

  wire alu_2_1_p1, alu_2_1_p2, alu_2_1_p3, alu_2_1_p4, and_1_out, and_2_out, and_4_out, and_5_out,
       clock_1_out, decoder_1_out0, decoder_1_out1, decoder_1_out2, decoder_1_out3, decoder_1_out4,
       decoder_1_out5, decoder_1_out6, decoder_1_out7, decoder_2_out0, decoder_2_out1, decoder_2_out2,
       decoder_2_out3, decoder_2_out4, decoder_2_out5, decoder_2_out6, decoder_2_out7, hef4014bp_1_q7,
       n74ls161_1_rco, n74ls161_3_rco, n74ls161_4_rco, n74ls195_1_nq3, n74ls195_2_nq3, not_1_out, not_2_out,
       not_3_out, not_4_out, not_5_out, not_6_out, not_15_out, not_16_out, not_17_out, not_18_out,
       not_19_out, not_20_out, not_21_out, not_22_out, or_1_out, or_2_out, or_3_out, pull_resistor_1_node,
       pull_resistor_2_node, pull_resistor_4_node;
  wire [3:0] n74ls161_1_data_out, n74ls161_2_data_out, n74ls161_3_data_out, n74ls161_4_data_out, undriven,
       undriven_2, undriven_3, undriven_4;
  wire [7:0] controlled_buffer_1_out, rom_1_data, undriven_5, undriven_6;

  not not_1 (not_1_out, in_1);
  Clock clock_1 (.out(clock_1_out));
  // ALU_2 alu_2_1: pin names not known; wires that end beside it: alu_2_1_p1, alu_2_1_p2, alu_2_1_p3, alu_2_1_p4
  _74ls195 u_74ls195_1 (.nQ3(n74ls195_1_nq3));  // open: Clock, clear, Parallel_In, J, Parallel_Load, Parallel_Out
  not not_2 (not_2_out, n74ls195_1_nq3);
  not not_3 (not_3_out, and_2_out);
  and and_1 (and_1_out, not_4_out, or_1_out);
  and and_2 (and_2_out, or_2_out, or_1_out);
  not not_4 (not_4_out, or_2_out);
  _74ls195 u_74ls195_2 (
    .J(not_2_out), .nQ3(n74ls195_2_nq3));  // open: Clock, clear, Parallel_In, Parallel_Load, Parallel_Out
  not not_5 (not_5_out, or_1_out);
  assign controlled_buffer_1_out = not_5_out ? undriven_5 : 8'bz;  // Controlled_Buffer controlled_buffer_1
  RAM #(.addrWidth(16), .bus("asynch")) ram_1 (
    .addr({undriven_4, undriven_3, undriven_2, undriven}), .data(controlled_buffer_1_out), .sel(not_3_out),
    .ld(and_1_out), .clr(not_1_out));
  or or_1 (or_1_out, pull_resistor_1_node, rom_1_data[6]);
  or or_2 (or_2_out, pull_resistor_2_node, rom_1_data[6]);
  not not_6 (not_6_out, n74ls195_2_nq3);
  assign controlled_buffer_1_out = rom_1_data[6] ? undriven_6 : 8'bz;  // Controlled_Buffer controlled_buffer_2
  Pull_Resistor #(.pull(1)) pull_resistor_1 (.node(pull_resistor_1_node));
  Pull_Resistor #(.pull(1)) pull_resistor_2 (.node(pull_resistor_2_node));
  Pull_Resistor #(.pull(1)) pull_resistor_3 (.node(rom_1_data[6]));
  hef4014bp hef4014bp_1 (
    .Data_In(controlled_buffer_1_out), .Serial_In(not_6_out), .Q7(hef4014bp_1_q7));  // open: Parallel_Enable, Clock, Q5, Q6
  _74ls161 u_74ls161_1 (
    .Count_Enable(n74ls161_3_rco), .nLoad(pull_resistor_4_node), .Clock(clock_1_out), .nClear(in_1),
    .Data_Out(n74ls161_1_data_out), .RCO(n74ls161_1_rco), .Data_Out_2(out_2));  // open: Data_In
  _74ls161 u_74ls161_2 (
    .Data_In(out_2), .Count_Enable(n74ls161_4_rco), .nLoad(pull_resistor_4_node), .Clock(clock_1_out),
    .nClear(in_1), .Data_Out(n74ls161_2_data_out), .Data_Out_2(out_4));  // open: RCO
  _74ls161 u_74ls161_3 (
    .Count_Enable(pull_resistor_4_node), .nLoad(pull_resistor_4_node), .Clock(clock_1_out), .nClear(in_1),
    .Data_Out(n74ls161_3_data_out), .RCO(n74ls161_3_rco), .Data_Out_2(out_3));  // open: Data_In
  _74ls161 u_74ls161_4 (
    .Data_In(out_3), .Count_Enable(n74ls161_1_rco), .nLoad(pull_resistor_4_node), .Clock(clock_1_out),
    .nClear(in_1), .Data_Out(n74ls161_4_data_out), .RCO(n74ls161_4_rco), .Data_Out_2(out_5));
  hef4014bp hef4014bp_2 (
    .Data_In({out_4, out_5}), .Serial_In(hef4014bp_1_q7));  // open: Parallel_Enable, Clock, Q5, Q6, Q7
  _74hc595 u_74hc595_1 ();  // open: Serial_Clk, Serial_In, nSerial_Clear, nOE, RClk, out_6, nQ7
  ROM #(.addrWidth(15)) rom_1 (
    .addr({n74ls161_2_data_out, n74ls161_4_data_out, n74ls161_1_data_out, n74ls161_3_data_out[3:1]}),
    .data(rom_1_data), .sel(1'b1));
  Pull_Resistor #(.pull(1)) pull_resistor_4 (.node(pull_resistor_4_node));
  and and_3 (pull_resistor_2_node, ~rom_1_data[6], rom_1_data[5], rom_1_data[4]);  // AND_Gate
  and and_4 (and_4_out, rom_1_data[6], n74ls161_3_data_out[0]);
  Decoder #(.select(3), .disabled(0)) decoder_1 (
    .out0(decoder_1_out0), .out1(decoder_1_out1), .out2(decoder_1_out2), .out3(decoder_1_out3),
    .out4(decoder_1_out4), .out5(decoder_1_out5), .out6(decoder_1_out6), .out7(decoder_1_out7),
    .sel(rom_1_data[6:4]), .en(rom_1_data[7]));
  // NOT_Gate not_7 has open pins: in=decoder_1_out5, out=open
  not not_8 (pull_resistor_4_node, decoder_1_out2);
  // NOT_Gate not_9 has open pins: in=decoder_1_out0, out=open
  not not_10 (pull_resistor_1_node, decoder_1_out3);
  // NOT_Gate not_11 has open pins: in=decoder_1_out1, out=open
  // NOT_Gate not_12 has open pins: in=decoder_1_out4, out=open
  // NOT_Gate not_13 has open pins: in=decoder_1_out6, out=open
  and and_5 (and_5_out, clock_1_out, n74ls161_3_data_out[0], rom_1_data[7]);
  Decoder #(.select(3), .disabled(0)) decoder_2 (
    .out0(decoder_2_out0), .out1(decoder_2_out1), .out2(decoder_2_out2), .out3(decoder_2_out3),
    .out4(decoder_2_out4), .out5(decoder_2_out5), .out6(decoder_2_out6), .out7(decoder_2_out7),
    .sel(rom_1_data[6:4]), .en(and_5_out));
  // NOT_Gate not_14 has open pins: in=decoder_1_out7, out=open
  not not_15 (not_15_out, decoder_2_out0);
  Controlled_Buffer controlled_buffer_3 (.in(not_15_out), .en(or_3_out));  // open: out
  or or_3 (or_3_out, rom_1_data[7], and_4_out, clock_1_out);
  not not_16 (not_16_out, decoder_2_out5);
  not not_17 (not_17_out, decoder_2_out6);
  not not_18 (not_18_out, decoder_2_out3);
  not not_19 (not_19_out, decoder_2_out1);
  not not_20 (not_20_out, decoder_2_out7);
  not not_21 (not_21_out, decoder_2_out2);
  not not_22 (not_22_out, decoder_2_out4);
  Controlled_Buffer controlled_buffer_4 (.in(not_19_out), .en(or_3_out));  // open: out
  Controlled_Buffer controlled_buffer_5 (.in(not_18_out), .en(or_3_out));  // open: out
  Controlled_Buffer controlled_buffer_6 (.in(not_21_out), .en(or_3_out));  // open: out
  Controlled_Buffer controlled_buffer_7 (.in(not_17_out), .en(or_3_out));  // open: out
  Controlled_Buffer controlled_buffer_8 (.in(not_22_out), .en(or_3_out));  // open: out
  Controlled_Buffer controlled_buffer_9 (.in(not_16_out), .en(or_3_out));  // open: out
  Controlled_Buffer controlled_buffer_10 (.in(not_20_out), .en(or_3_out));  // open: out
  Pull_Resistor pull_resistor_5 (.node(or_3_out));

  // Notes on the sheet:
  //   RAM ADDRESS
  //   RAM WRITE BYTE
  //   RAM READ BYTE
  //   MSB PC Read
  //   contents of rom_1 (hex, n*v repeats v):
  //   d1 0 0 d4 b0
endmodule

module _74hc595 (
  input  Serial_Clk,
  input  Serial_In,
  input  nSerial_Clear,
  input  nOE,
  input  RClk,
  output [7:0] out_6,
  output nQ7
);

  wire not_1_out;
  wire [7:0] d_ff_8_q, register_1_q;

  D_Flip_Flop d_ff_1 (.D(Serial_In), .Q(d_ff_8_q[7]), .reset(nSerial_Clear));  // open: clk, Qn, preset, en
  D_Flip_Flop d_ff_2 (.D(d_ff_8_q[7]), .Q(d_ff_8_q[6]), .reset(nSerial_Clear));  // open: clk, Qn, preset, en
  D_Flip_Flop d_ff_3 (.D(d_ff_8_q[6]), .Q(d_ff_8_q[5]), .reset(nSerial_Clear));  // open: clk, Qn, preset, en
  D_Flip_Flop d_ff_4 (.D(d_ff_8_q[5]), .Q(d_ff_8_q[4]), .reset(nSerial_Clear));  // open: clk, Qn, preset, en
  D_Flip_Flop d_ff_5 (.D(d_ff_8_q[4]), .Q(d_ff_8_q[3]), .reset(nSerial_Clear));  // open: clk, Qn, preset, en
  D_Flip_Flop d_ff_6 (
    .clk(Serial_Clk), .D(d_ff_8_q[3]), .Q(d_ff_8_q[2]), .reset(nSerial_Clear));  // open: Qn, preset, en
  D_Flip_Flop d_ff_7 (
    .clk(Serial_Clk), .D(d_ff_8_q[2]), .Q(d_ff_8_q[1]), .reset(nSerial_Clear));  // open: Qn, preset, en
  D_Flip_Flop d_ff_8 (
    .clk(Serial_Clk), .D(d_ff_8_q[1]), .Q(d_ff_8_q[0]), .reset(nSerial_Clear));  // open: Qn, preset, en
  Register register_1 (.D(d_ff_8_q), .Q(register_1_q), .clk(RClk));  // open: en, clr
  not not_1 (not_1_out, nOE);
  assign out_6 = not_1_out ? register_1_q : 8'bz;  // Controlled_Buffer controlled_buffer_1
  not not_2 (nQ7, register_1_q[7]);
endmodule

module processor_6_with_actual_74_series (
);

  // _74xx590 74xx590_1: pin names not known
  // _74161 74161_1: pin names not known
  // _74161 74161_2: pin names not known
  // _74161 74161_3: pin names not known
  // _74161 74161_4: pin names not known
endmodule
